# Fritzing sketch Sketch (saved by Fritzing 0.9.3b)
breadboards: 1

parts:
  N-MOSFET = Basic FET N-Channel [package="D2Pak [SMD]"]
  atTiny85 = attiny85 [package=dip]
  220_Ohm_Resistor = Resistor [tolerance=±5% resistance=220 package=THT]
  220_Ohm_Resistor1 = Resistor [tolerance=±5% resistance=100 package=THT]
  Bauteil1 = Arduino Uno (Rev3)
  GSM_Shield = Arduino Cellular Shield
  HX711 = HX711 Weighing Sensor Module
  LOAD_CELL = IC, DIP package, 4 pins [chip_label="Load Cell"]
  6V_4x_AA = Battery
  VCC3 = Battery  # not connected
  Low_Power_Low_Dropout = KA78R05 Low Dropout Voltage Regulator [part_number=LP2950CZ-5.0 package=TO-220F-4L]  # not connected

nets:
  N1: N-MOSFET.Gate, 220_Ohm_Resistor.Pin_1
  N2: N-MOSFET.drain, Bauteil1.GND, HX711.E-
  N3: N-MOSFET.source, atTiny85.Pin_4, 220_Ohm_Resistor1.Pin_0, 6V_4x_AA.-
  N4: atTiny85.Pin_5, 220_Ohm_Resistor.Pin_0, 220_Ohm_Resistor1.Pin_1
  N5: atTiny85.Pin_6, Bauteil1.D2
  N6: atTiny85.Pin_8, 6V_4x_AA.+
  N7: Bauteil1.D8, GSM_Shield.D8
  N8: Bauteil1.D9_PWM, GSM_Shield.D9
  N9: Bauteil1.D5_PWM, HX711.A+
  N10: Bauteil1.D6_PWM, HX711.A-
  N11: Bauteil1.D7, GSM_Shield.D7
  N12: Bauteil1.3V3, HX711.E+
  N13: HX711.VCC, LOAD_CELL.pin3
  N14: HX711.GND, LOAD_CELL.pin1
  N15: HX711.DO/RX, LOAD_CELL.pin2
  N16: HX711.CK/TX, LOAD_CELL.pin4

notes:
  PWR -> ARDUINO
  GSM Shield
